// Logisim project 03 - Comparador - Igualdade - 8 bits.circ as structural Verilog: 1 circuit, main circuit main
module main (
  input  A0,
  input  B0,
  input  A1,
  input  B1,
  input  A2,
  input  B2,
  input  A3,
  input  B3,
  input  A4,
  input  B4,
  input  A5,
  input  B5,
  input  A6,
  input  B6,
  input  A7,
  input  B7
);

  wire and_1_out, and_2_out, and_3_out, xnor_1_out, xnor_2_out, xnor_3_out, xnor_4_out, xnor_5_out,
       xnor_6_out, xnor_7_out, xnor_8_out;

  xnor xnor_1 (xnor_1_out, A0, B0);
  xnor xnor_2 (xnor_2_out, A1, B1);
  xnor xnor_3 (xnor_3_out, A2, B2);
  xnor xnor_4 (xnor_4_out, A3, B3);
  xnor xnor_5 (xnor_5_out, A4, B4);
  xnor xnor_6 (xnor_6_out, A5, B5);
  xnor xnor_7 (xnor_7_out, A6, B6);
  xnor xnor_8 (xnor_8_out, A7, B7);
  and and_1 (and_1_out, xnor_1_out, xnor_2_out, xnor_3_out, xnor_4_out);
  and and_2 (and_2_out, xnor_5_out, xnor_6_out, xnor_7_out, xnor_8_out);
  and and_3 (and_3_out, and_1_out, and_2_out);
  LED led_1 (.in(and_3_out));
endmodule
