// Logisim project 06 - Decodificador 3x8.circ as structural Verilog: 1 circuit, main circuit main
module main (
  input  A,
  input  B,
  input  C
);

  wire and_1_out, and_2_out, and_3_out, and_4_out, and_5_out, and_6_out, and_7_out, and_8_out, not_1_out,
       not_2_out, not_3_out;

  not not_1 (not_1_out, A);
  not not_2 (not_2_out, B);
  not not_3 (not_3_out, C);
  and and_1 (and_1_out, not_1_out, not_2_out, not_3_out);
  and and_2 (and_2_out, not_1_out, not_2_out, C);
  and and_3 (and_3_out, not_1_out, B, not_3_out);
  and and_4 (and_4_out, not_1_out, B, C);
  and and_5 (and_5_out, A, not_2_out, not_3_out);
  and and_6 (and_6_out, A, not_2_out, C);
  and and_7 (and_7_out, A, B, not_3_out);
  and and_8 (and_8_out, A, B, C);
  LED D0 (.in(and_1_out));
  LED D1 (.in(and_2_out));
  LED D2 (.in(and_3_out));
  LED D3 (.in(and_4_out));
  LED D4 (.in(and_5_out));
  LED D5 (.in(and_6_out));
  LED D6 (.in(and_7_out));
  LED D7 (.in(and_8_out));

  // Notes on the sheet:
  //   msb -> A   B   C <- lsb
  //   Decodificador 3 x 8
endmodule
