// Logisim project 08 - shifter1-bit left-right.circ as structural Verilog: 1 circuit, main circuit main
module main (
  input  D0,
  input  D1,
  input  D2,
  input  D3,
  input  D4,
  input  D5,
  input  D6,
  input  D7,
  input  C
);

  wire and_1_out, and_2_out, and_3_out, and_4_out, and_5_out, and_6_out, and_7_out, and_8_out, and_9_out,
       and_10_out, and_11_out, and_12_out, and_13_out, and_14_out, not_1_out, or_1_out, or_2_out, or_3_out,
       or_4_out, or_5_out, or_6_out;

  not not_1 (not_1_out, C);
  and and_1 (and_1_out, D0, C);
  LED S0 (.in(and_2_out));
  and and_2 (and_2_out, not_1_out, D1);
  and and_3 (and_3_out, D1, C);
  or or_1 (or_1_out, and_1_out, and_4_out);
  LED S1 (.in(or_1_out));
  and and_4 (and_4_out, not_1_out, D2);
  and and_5 (and_5_out, D2, C);
  or or_2 (or_2_out, and_3_out, and_6_out);
  LED S2 (.in(or_2_out));
  and and_6 (and_6_out, not_1_out, D3);
  or or_3 (or_3_out, and_5_out, and_8_out);
  and and_7 (and_7_out, D3, C);
  LED S3 (.in(or_3_out));
  and and_8 (and_8_out, not_1_out, D4);
  or or_4 (or_4_out, and_7_out, and_10_out);
  and and_9 (and_9_out, D4, C);
  LED S4 (.in(or_4_out));
  and and_10 (and_10_out, not_1_out, D5);
  or or_5 (or_5_out, and_9_out, and_12_out);
  LED S5 (.in(or_5_out));
  and and_11 (and_11_out, D5, C);
  and and_12 (and_12_out, not_1_out, D6);
  or or_6 (or_6_out, and_11_out, and_14_out);
  LED S6 (.in(or_6_out));
  and and_13 (and_13_out, D6, C);
  and and_14 (and_14_out, not_1_out, D7);
  LED S7 (.in(and_13_out));

  // Notes on the sheet:
  //   C = 0 para a esquerda, 1 para a direita 
  //   lsb ->
  //   lsb ->
  //   Shifter 1 Bit
  //   msb ->
  //   D7 D6 D5 D4 D3 D2 D1 D0
  //   S7 S6 S5 S4 S3 S2 S1 S0
  //   Bit deslocado para a esquerda = multiplicação por 2
  //   Bit deslocado para a direita = divisão por 2
  //   <- lsb
  //   <-msb
endmodule
