// Logisim project alu-1bit.circ as structural Verilog: 1 circuit, main circuit main
module main (
  input  INVA,
  input  A,
  input  ENA,
  input  B,
  input  ENB
);

  wire and_1_out, and_2_out, xor_1_out;

  xor xor_1 (xor_1_out, INVA, and_1_out);
  and and_1 (and_1_out, A, ENA);
  and and_2 (and_2_out, B, ENB);
  // NOT_Gate not_1 has open pins: in=and_2_out, out=open
  // AND_Gate and_3 has open pins: in0=xor_1_out, in1=and_2_out, out=open
  // OR_Gate or_1 has open pins: in0=xor_1_out, in1=and_2_out, out=open
endmodule
