// Logisim project 07 - Mux 8 bits.circ as structural Verilog: 1 circuit, main circuit main
module main (
  input  D0,
  input  D1,
  input  D2,
  input  D3,
  input  D4,
  input  D5,
  input  D6,
  input  D7,
  input  A,
  input  B,
  input  C
);

  wire and_1_out, and_2_out, and_3_out, and_4_out, and_5_out, and_6_out, and_7_out, and_8_out, not_1_out,
       not_2_out, not_3_out, or_1_out;

  not not_1 (not_1_out, A);
  not not_2 (not_2_out, B);
  not not_3 (not_3_out, C);
  and and_1 (and_1_out, D0, not_1_out, not_2_out, not_3_out);
  and and_2 (and_2_out, D1, not_1_out, not_2_out, C);
  and and_3 (and_3_out, D2, not_1_out, B, not_3_out);
  and and_4 (and_4_out, D3, not_1_out, B, C);
  and and_5 (and_5_out, D4, A, not_2_out, not_3_out);
  and and_6 (and_6_out, D5, A, not_2_out, C);
  and and_7 (and_7_out, D6, A, B, not_3_out);
  and and_8 (and_8_out, D7, A, B, C);
  or or_1 (or_1_out, and_1_out, and_2_out, and_3_out, and_4_out, and_5_out, and_6_out, and_7_out, and_8_out);
  LED F (.in(or_1_out));

  // Notes on the sheet:
  //   msb -> A   B   C <- lsb
  //   Mux 8 entradas
endmodule
