// Logisim project senha_8bits.circ as structural Verilog: 1 circuit, main circuit main
module main (
  input  in_1,
  input  in_2,
  input  in_3,
  input  in_4,
  input  in_5,
  input  in_6,
  input  in_7,
  input  in_8,
  input  in_9,
  input  in_10,
  input  in_11,
  input  in_12,
  input  in_13,
  input  in_14,
  input  in_15,
  input  in_16
);

  wire and_1_out, and_2_out, and_3_out, and_4_out, not_1_out, not_2_out, not_3_out, not_4_out, not_5_out,
       not_6_out, not_7_out, not_8_out;

  not not_1 (not_1_out, in_2);
  not not_2 (not_2_out, in_3);
  not not_3 (not_3_out, in_5);
  not not_4 (not_4_out, in_8);
  not not_5 (not_5_out, in_10);
  not not_6 (not_6_out, in_11);
  not not_7 (not_7_out, in_13);
  not not_8 (not_8_out, in_16);
  and and_1 (and_1_out, in_1, in_4, in_6, in_7);
  and and_2 (and_2_out, not_2_out, not_1_out, not_3_out, not_4_out);
  and and_3 (and_3_out, and_1_out, and_2_out);
  and and_4 (and_4_out, in_9, in_12, in_14, in_15, not_6_out, not_5_out, not_7_out, not_8_out);
  LED led_1 (.in(and_3_out));
  LED led_2 (.in(and_4_out));
endmodule
