// Logisim project soma-4bits.circ as structural Verilog: 1 circuit, main circuit main
module main (
  input  A0,
  input  B0,
  input  A1,
  input  B1,
  input  A2,
  input  B2,
  input  A3,
  input  B3,
  output out_9,
  output out_10,
  output out_11,
  output out_12,
  output out_13
);

  wire and_1_out, and_2_out, and_3_out, and_4_out, and_5_out, and_6_out, and_7_out, xor_2_out, xor_4_out,
       xor_6_out, xor_7_out, xor_9_out;

  and and_1 (and_1_out, B0, A0);
  and and_2 (and_2_out, B1, A1);
  and and_3 (and_3_out, xor_2_out, and_1_out);
  and and_4 (and_4_out, xor_6_out, xor_4_out);
  and and_5 (and_5_out, B2, A2);
  and and_6 (and_6_out, xor_9_out, xor_7_out);
  and and_7 (and_7_out, B3, A3);
  xor xor_1 (out_9, A0, B0);
  xor xor_2 (xor_2_out, A1, B1);
  xor xor_3 (out_10, and_1_out, xor_2_out);
  xor xor_4 (xor_4_out, and_2_out, and_3_out);
  xor xor_5 (out_11, xor_4_out, xor_6_out);
  xor xor_6 (xor_6_out, A2, B2);
  xor xor_7 (xor_7_out, and_4_out, and_5_out);
  xor xor_8 (out_12, xor_7_out, xor_9_out);
  xor xor_9 (xor_9_out, A3, B3);
  xor xor_10 (out_13, and_6_out, and_7_out);
endmodule
